# Fritzing sketch Uno (saved by Fritzing 0.8.5b)
circuit board: 8.46667cm x 5.64444cm
breadboards: 1

parts:
  Composants1 = Arduino Uno (Rev3)
  LCD1 = LCD screen
  R1 = Trimmer Potentiometer [maximum_resistance=10kΩ package=THT]
  S1 = Pushbutton [package="[THT]"]
  S2 = Pushbutton [package="[THT]"]
  S3 = Pushbutton [package="[THT]"]
  S4 = Pushbutton [package="[THT]"]
  S5 = Pushbutton [package="[THT]"]
  S6 = Pushbutton [package="[THT]"]
  R2 = Resistor [tolerance=±5% resistance=220 package=THT]

nets:
  N1: Composants1.D8, LCD1.DB4
  N2: Composants1.D9_PWM, LCD1.DB5
  N3: Composants1.D10_PWM/SS, LCD1.DB6
  N4: Composants1.D11_PWM/MOSI, LCD1.DB7
  N5: Composants1.D12/MISO, S5.Pin_3, S5.Pin_4
  N6: Composants1.D13/SCK, S4.Pin_3, S4.Pin_4
  GND: Composants1.GND, LCD1.VSS, LCD1.R/W, LCD1.LED-, R1.leg2, S1.Pin_3, S1.Pin_4, S2.Pin_3, S2.Pin_4, S3.Pin_3, S3.Pin_4, S4.Pin_1, S4.Pin_2, S5.Pin_1, S5.Pin_2, S6.Pin_1, S6.Pin_2
  N7: Composants1.D2, S1.Pin_1, S1.Pin_2
  N8: Composants1.D3_PWM, S2.Pin_1, S2.Pin_2
  N9: Composants1.D4, S3.Pin_1, S3.Pin_2, S6.Pin_3, S6.Pin_4
  N10: Composants1.D6_PWM, LCD1.RS
  N11: Composants1.D7, LCD1.E
  5V: Composants1.5V, LCD1.VDD, R1.leg1, R2.Pin_1
  N12: LCD1.V0, R1.wiper
  N13: LCD1.LED+, R2.Pin_0
